// Logisim project vhdl_assignment2.circ as structural Verilog
module main (
  input  in_1,
  input  in_2,
  input  in_3,
  input  in_4,
  input  in_5,
  input  in_6,
  input  in_7,
  input  in_8,
  input  in_9,
  input  in_10,
  input  in_11,
  input  in_12,
  input  [2:0] in_13,
  input  en,
  input  [3:0] dat,
  input  [24:0] vt,
  input  [12:0] in_17,
  input  in_18,
  output out_19,
  output out_20,
  output out_21
);

  wire vote25_1_result;
  wire [7:0] count13_1_display, led_letters_1_display;

  led_letters led_letters_1 (.en(en), .dat(dat), .display(led_letters_1_display));
  vote25 vote25_1 (.vt(vt), .result(vote25_1_result));
  count13 count13_1 (.vt(in_17), .en(in_18), .display(count13_1_display));
  andor andor_1 (.a(in_1), .b(in_2), .c(in_3), .d(in_4), .out1(out_19), .out2(out_20));
  LED result (.in(vote25_1_result));
  mux8_1 mux8_1_1 (
    .a(in_5), .b(in_6), .c(in_7), .d(in_8), .e(in_9), .f(in_10), .g(in_11), .h(in_12), .ch(in_13),
    .data(out_21));
  _7_Segment_Display u_7_segment_display_1 (
    .g(led_letters_1_display[1]), .f(led_letters_1_display[2]), .a(led_letters_1_display[7]),
    .b(led_letters_1_display[6]), .e(led_letters_1_display[3]), .d(led_letters_1_display[4]),
    .c(led_letters_1_display[5]), .dp(led_letters_1_display[0]));
  _7_Segment_Display u_7_segment_display_2 (
    .g(count13_1_display[1]), .f(count13_1_display[2]), .a(count13_1_display[7]), .b(count13_1_display[6]),
    .e(count13_1_display[3]), .d(count13_1_display[4]), .c(count13_1_display[5]), .dp(count13_1_display[0]));
endmodule

// VHDL entity andor, as the project stores it:
library ieee;
use ieee.std_logic_1164.all;
use ieee.std_logic_arith.all;
use ieee.std_logic_unsigned.all;

entity andor is
    port(
        a, b, c, d : in std_logic;
        out1, out2 : out std_logic
    );
end entity andor;

architecture bhv of andor is
begin
    out1 <= a and b and c and d;
    out2 <= a or b or c or d;
end architecture bhv;

// VHDL entity mux8_1, as the project stores it:
library ieee;
use ieee.std_logic_1164.all;
use ieee.std_logic_arith.all;
use ieee.std_logic_unsigned.all;

entity mux8_1 is
    port(
        a, b, c, d, e, f, g, h : in std_logic;
        ch : in std_logic_vector(2 downto 0);
        data : out std_logic
    );
end entity mux8_1;

architecture bhv of mux8_1 is
begin
    process(a, b, c, d, e, f, g, h, ch)
    begin
        case ch is
            when "000" => data <= a;
            when "001" => data <= b;
            when "010" => data <= c;
            when "011" => data <= d;
            when "100" => data <= e;
            when "101" => data <= f;
            when "110" => data <= g;
            when "111" => data <= h;
            when others => data <= '0';
        end case;
    end process;
end architecture bhv;

// VHDL entity led_letters, as the project stores it:
library ieee;
use ieee.std_logic_1164.all;

entity led_letters is
    port(
        en      : in std_logic;
        dat     : in std_logic_vector(3 downto 0);
        display : out std_logic_vector(7 downto 0)
    );
end entity led_letters;

architecture bhv of led_letters is
begin
    process(en, dat)
    begin
        if en = '0' then
            display <= "ZZZZZZZZ";
        else
            case dat is
                when "0000" => display <= "11101110";
                when "0001" => display <= "00111110";
                when "0010" => display <= "00011010";
                when "0011" => display <= "01111010";
                when "0100" => display <= "10001110";
                when "0101" => display <= "10111110";
                when others => display <= "00000000";
            end case;
        end if;
    end process;
end architecture bhv;

// VHDL entity vote25, as the project stores it:
library ieee;
use ieee.std_logic_1164.all;
use ieee.std_logic_arith.all;
use ieee.std_logic_unsigned.all;

entity vote25 is
    port(
        vt : in std_logic_vector(25 downto 1);
        result : out std_logic
    );
end entity vote25;

architecture bhv of vote25 is
begin
    process(vt)
        variable sum : integer range 0 to 25;
    begin
        sum := 0;

        for i in 1 to 25 loop
            if vt(i) = '1' then
                sum := sum + 1;
            end if;
        end loop;

        if sum > 12 then
            result <= '1';
        else
            result <= '0';
        end if;
    end process;
end architecture bhv;

// VHDL entity count13, as the project stores it:
library ieee;
use ieee.std_logic_1164.all;
use ieee.std_logic_arith.all;
use ieee.std_logic_unsigned.all;

entity count13 is
    port(
        vt      : in std_logic_vector(12 downto 0);
        en      : in std_logic;
        display : out std_logic_vector(7 downto 0)
    );
end entity count13;

architecture bhv of count13 is
begin
    process(vt, en)
        variable sum : integer range 0 to 15;
    begin
        sum := 0;

        for i in 0 to 12 loop
            if vt(i) = '1' then
                sum := sum + 1;
            end if;
        end loop;

        if en = '0' then
            display <= "ZZZZZZZZ";

        else
            case sum is
                when 0  => display <= "11111100";
                when 1  => display <= "01100000";
                when 2  => display <= "11011010";
                when 3  => display <= "11110010";
                when 4  => display <= "01100110";
                when 5  => display <= "10110110";
                when 6  => display <= "10111110";
                when 7  => display <= "11100000";
                when 8  => display <= "11111110";
                when 9  => display <= "11100110";

                when 10 => display <= "11101110"; -- A
                when 11 => display <= "00111110"; -- b
                when 12 => display <= "10011100"; -- C
                when 13 => display <= "01111010"; -- d
                when 14 => display <= "10011110"; -- E
                when 15 => display <= "10001110"; -- F

                when others =>
                    display <= "00000000";
            end case;
        end if;

    end process;
end architecture bhv;
